# Fritzing sketch magsensor (saved by Fritzing 0.9.2b)
breadboards: 1

parts:
  Part1 = Arduino Uno (Rev3)
  U1 = RF-LINK_TX [package=rf-link_tx]
  Magnetic_Switch = SWITCH-MOMENTARY-2 [package=tactile-pth]
  R1 = Resistor [tolerance=±5% resistance=47k package="2010 [SMD]"]

nets:
  N1: Part1.D10_PWM/SS, U1.+5V
  N2: Part1.D13/SCK, U1.DATA
  GND: Part1.GND, U1.GND, R1.Pin_1
  N3: Part1.D2, Magnetic_Switch.2, R1.Pin_0
  N4: Part1.5V, Magnetic_Switch.1
